// Logisim project ex5.circ as structural Verilog: 1 circuit, main circuit main
module main (
  input  X1,
  input  X2,
  input  X3,
  input  X4,
  output Sa,
  output Sb,
  output Sc,
  output Sd,
  output Se,
  output Sf,
  output Sg
);

  wire and_1_out, and_2_out, and_3_out, and_4_out, and_5_out, and_6_out, and_7_out, and_8_out, and_9_out,
       and_10_out, and_11_out, and_12_out, and_13_out, and_14_out, and_15_out, and_16_out, and_17_out,
       and_18_out, and_19_out, and_20_out, and_21_out, not_1_out, not_2_out, not_3_out, not_4_out;

  not not_1 (not_1_out, X1);
  not not_2 (not_2_out, X2);
  not not_3 (not_3_out, X3);
  not not_4 (not_4_out, X4);
  and and_1 (and_1_out, not_1_out, X3);
  and and_2 (and_2_out, not_1_out, not_2_out);
  and and_3 (and_3_out, not_1_out, X2);
  and and_4 (and_4_out, X1, not_2_out, not_3_out);
  and and_5 (and_5_out, not_2_out, not_3_out);
  and and_6 (and_6_out, not_1_out, not_3_out);
  and and_7 (and_7_out, not_1_out, X4);
  and and_8 (and_8_out, and_2_out, not_4_out);
  and and_9 (and_9_out, and_3_out, X4);
  and and_10 (and_10_out, and_1_out, X4);
  and and_11 (and_11_out, and_6_out, not_4_out);
  and and_12 (and_12_out, and_5_out, not_4_out);
  and and_13 (and_13_out, and_6_out, X2, X4);
  and and_14 (and_14_out, and_1_out, not_2_out);
  and and_15 (and_15_out, and_1_out, not_4_out);
  and and_16 (and_16_out, X1, and_5_out);
  and and_17 (and_17_out, and_6_out, not_4_out);
  and and_18 (and_18_out, and_6_out, X2);
  and and_19 (and_19_out, and_3_out, not_4_out);
  and and_20 (and_20_out, and_1_out, not_2_out);
  and and_21 (and_21_out, and_6_out, X2);
  or or_1 (Sa, and_1_out, and_8_out, and_9_out, and_4_out);
  or or_2 (Sb, and_2_out, and_5_out, and_10_out, and_11_out);
  or or_3 (Sc, and_3_out, and_5_out, and_7_out);
  or or_4 (Sd, and_12_out, and_13_out, and_14_out, and_15_out);
  or or_5 (Se, and_12_out, and_15_out);
  or or_6 (Sf, and_16_out, and_17_out, and_18_out, and_19_out);
  or or_7 (Sg, and_15_out, and_20_out, and_16_out, and_21_out);

  // Notes on the sheet:
  //   -X1X3
  //   -X1-X2
  //   -X1X2
  //   X1-X2-X3
  //   -X1-X3
  //   -X2-X3
endmodule
